# Fritzing sketch PythagoraPlayer (saved by Fritzing 0.9.2b)
circuit board: 8.46667cm x 5.64444cm
breadboards: 1

parts:
  パーツ1 = Arduino Uno (Rev3)
  J1 = Piezo Speaker
  S1 = Round Pushbutton
  R1 = Resistor [tolerance=±5% resistance=220 package=THT]

nets:
  N1: パーツ1.D8, S1.leg1, R1.Pin_0
  N2: パーツ1.D12/MISO, J1.pin2
  GND: パーツ1.GND, J1.pin1, R1.Pin_1
  N3: パーツ1.5V, S1.leg0

// code stored in the sketch: PythagoraPlayer.ino
/*
 * PythagoraPlayer
 */

#define SPEAKER_PIN 12
#define BUTTON_PIN   8

#define TONE3_A  220  // A3
#define TONE3_B  247  // B3
#define TONE4_C  262  // C4
#define TONE4_CS 277  // C4#
#define TONE4_D  294  // D4
#define TONE4_E  330  // E4
#define TONE4_F  349  // F4
#define TONE4_FS 370  // F4#
#define TONE4_G  392  // G4
#define TONE4_A  440  // A4
#define TONE4_B  494  // B4
#define TONE5_C  523  // C5

int score[] = {
  TONE4_D, TONE4_E, TONE4_D, TONE4_E, TONE4_G, TONE4_FS,TONE4_D, TONE4_E,
  TONE4_D, TONE4_E, TONE4_D, TONE4_E, TONE5_C, TONE4_B, TONE4_G, TONE4_A,
  TONE4_D, TONE4_E, TONE4_D, TONE4_E, TONE4_G, TONE4_FS,TONE4_D, TONE4_E,
  TONE3_B, TONE3_A, TONE3_B, TONE4_C, TONE4_CS,TONE4_D, TONE4_D,
  TONE4_D, TONE4_E, TONE4_D, TONE4_E, TONE4_G, TONE4_FS,TONE4_D, TONE4_E,
  TONE4_D, TONE4_E, TONE4_D, TONE4_E, TONE5_C, TONE4_B, TONE4_G, TONE4_A,
  TONE4_D, TONE4_E, TONE4_D, TONE4_E, TONE4_G, TONE4_FS,TONE4_D, TONE4_E,
  TONE3_B, TONE3_A,
  TONE4_E, TONE4_E, TONE4_FS,TONE4_E, TONE4_FS,TONE4_G, TONE4_D, TONE3_B,
  TONE4_C, TONE4_C, TONE4_D, TONE4_C, TONE4_D, TONE3_B,
  TONE4_D, TONE4_E, TONE4_D, TONE4_E, TONE4_G, TONE4_FS,TONE4_D, TONE4_E,
  TONE4_D, TONE4_E, TONE4_D, TONE4_E, TONE4_G, TONE4_FS,TONE4_D, TONE4_E,
  TONE4_D, TONE4_E, TONE4_D, TONE4_E, TONE5_C, TONE4_B, TONE4_G,
  TONE4_D, TONE4_E, TONE4_D, TONE4_E, TONE5_C, TONE4_B, TONE4_G
};

int scoreLength;
int sequencer;
bool beep;

void setup() {
  pinMode(SPEAKER_PIN, OUTPUT);
  pinMode(BUTTON_PIN, INPUT);

  scoreLength = sizeof(score) / sizeof(int);
  sequencer = 0;
  beep = false;
}

void loop() {
  int result = LOW;
  int lastResult = LOW;
  int count = 0;

  do {
    result = digitalRead(BUTTON_PIN);
    if(result == lastResult) {
      count++;
    } else {
      lastResult = result;
      count = 0;
    }
    delay(1);
  } while(count < 10);

  if (lastResult == HIGH) {
    tone(SPEAKER_PIN, score[sequencer]);
    beep = true;
  } else {
    noTone(SPEAKER_PIN);
    if (beep) {
      beep = false;
      sequencer++;
      if (sequencer >= scoreLength) {
        sequencer = 0;
      }
    }
  }
}
